// Logisim project ICS233_PROJECT.circ as structural Verilog: 12 circuits, main circuit Register_File
module Register_File (
  input  [15:0] BusW,
  input  [2:0] Rs1,
  input  [2:0] RD,
  input  [2:0] Rs2,
  input  RegWrite,
  input  Cllock,
  output [15:0] BusA,
  output [15:0] BusB
);

  wire and_1_out, and_2_out, and_3_out, and_4_out, and_5_out, and_6_out, and_7_out, and_8_out,
       decoder_1_out0, decoder_1_out1, decoder_1_out2, decoder_1_out3, decoder_1_out4, decoder_1_out5,
       decoder_1_out6, decoder_1_out7;
  wire [15:0] register_1_q, register_2_q, register_3_q, register_4_q, register_5_q, register_6_q,
       register_7_q, register_8_q;

  Decoder #(.select(3), .enable("false")) decoder_1 (
    .out0(decoder_1_out0), .out1(decoder_1_out1), .out2(decoder_1_out2), .out3(decoder_1_out3),
    .out4(decoder_1_out4), .out5(decoder_1_out5), .out6(decoder_1_out6), .out7(decoder_1_out7), .sel(RD));
  and and_1 (and_1_out, decoder_1_out0, RegWrite);
  and and_2 (and_2_out, decoder_1_out1, RegWrite);
  and and_3 (and_3_out, decoder_1_out2, RegWrite);
  and and_4 (and_4_out, decoder_1_out3, RegWrite);
  and and_5 (and_5_out, decoder_1_out4, RegWrite);
  and and_6 (and_6_out, decoder_1_out5, RegWrite);
  and and_7 (and_7_out, decoder_1_out6, RegWrite);
  and and_8 (and_8_out, decoder_1_out7, RegWrite);
  Register #(.width(16)) register_1 (.D({16{1'b0}}), .en(and_1_out), .Q(register_1_q), .clk(Cllock), .clr(1'b0));
  Register #(.width(16)) register_2 (.D(BusW), .en(and_2_out), .Q(register_2_q), .clk(Cllock), .clr(1'b0));
  Register #(.width(16)) register_3 (.D(BusW), .en(and_3_out), .Q(register_3_q), .clk(Cllock), .clr(1'b0));
  Register #(.width(16)) register_4 (.D(BusW), .en(and_4_out), .Q(register_4_q), .clk(Cllock), .clr(1'b0));
  Register #(.width(16)) register_5 (.D(BusW), .en(and_5_out), .Q(register_5_q), .clk(Cllock), .clr(1'b0));
  Register #(.width(16)) register_6 (.D(BusW), .en(and_6_out), .Q(register_6_q), .clk(Cllock), .clr(1'b0));
  Register #(.width(16)) register_7 (.D(BusW), .en(and_7_out), .Q(register_7_q), .clk(Cllock), .clr(1'b0));
  Register #(.width(16)) register_8 (.D(BusW), .en(and_8_out), .Q(register_8_q), .clk(Cllock), .clr(1'b0));
  Multiplexer #(.select(3), .width(16)) multiplexer_1 (
    .in0(register_1_q), .in1(register_2_q), .in2(register_3_q), .in3(register_4_q), .in4(register_5_q),
    .in5(register_6_q), .in6(register_7_q), .out(BusA), .sel(Rs1));  // open: in7, en
  Multiplexer #(.select(3), .width(16)) multiplexer_2 (
    .in0(register_1_q), .in1(register_2_q), .in2(register_3_q), .in3(register_4_q), .in4(register_5_q),
    .in5(register_6_q), .in6(register_7_q), .in7(register_8_q), .out(BusB), .sel(Rs2));  // open: en
endmodule

module Logic_Gate (
  input  [15:0] in_1,
  input  [15:0] in_2,
  input  [1:0] F,
  output [15:0] \output 
);

  wire [15:0] and_1_out, or_1_out, xor_1_out;

  assign and_1_out = in_1 & in_2;  // AND_Gate and_1, 16 bits wide
  assign or_1_out = in_1 | in_2;  // OR_Gate or_1, 16 bits wide
  assign xor_1_out = in_1 ^ in_2;  // XOR_Gate xor_1, 16 bits wide
  Multiplexer #(.select(2), .width(16)) multiplexer_1 (
    .in0(xor_1_out), .in1(or_1_out), .in2(and_1_out), .out(\output ), .sel(F));  // open: in3, en

  // Notes on the sheet:
  //   A
  //   B
endmodule

module Arithematic (
  input  [15:0] in_1,
  input  [15:0] in_2,
  input  [1:0] F,
  output [15:0] Output
);

  wire comparator_1_lt, comparator_2_lt;
  wire [15:0] adder_1_out, bit_extender_1_out, bit_extender_2_out, bit_extender_3_out, xor_1_out;

  assign bit_extender_1_out = {{15{F[0]}}, F[0]};  // Bit_Extender bit_extender_1
  assign xor_1_out = in_2 ^ bit_extender_1_out;  // XOR_Gate xor_1, 16 bits wide
  Adder #(.width(16)) adder_1 (.a(in_1), .b(xor_1_out), .out(adder_1_out));  // open: cin, cout
  Comparator #(.width(16)) comparator_1 (.a(in_1), .b(in_1), .lt(comparator_1_lt));  // open: gt, eq
  Comparator #(.width(16), .mode("unsigned")) comparator_2 (.a(in_1), .b(in_2), .lt(comparator_2_lt));  // open: gt, eq
  assign bit_extender_2_out = {{15{1'b0}}, comparator_1_lt};  // Bit_Extender bit_extender_2
  assign bit_extender_3_out = {{15{1'b0}}, comparator_2_lt};  // Bit_Extender bit_extender_3
  Multiplexer #(.select(2), .width(16), .enable("false")) multiplexer_1 (
    .in0(adder_1_out), .in1(adder_1_out), .in2(bit_extender_2_out), .in3(bit_extender_3_out), .out(Output),
    .sel(F));

  // Notes on the sheet:
  //   A
  //   B
endmodule

module Shifter (
  input  [15:0] in_1,
  input  [15:0] in_2,
  input  [1:0] F,
  output [15:0] Output
);

  wire [3:0] bit_extender_1_out;
  wire [15:0] shifter_1_out, shifter_2_out, shifter_3_out;

  Bit_Extender #(.in_width(16), .out_width(4)) bit_extender_1 (.in(in_2), .out(bit_extender_1_out));
  Shifter_part #(.width(16)) shifter_1 (.in(in_1), .\dist (bit_extender_1_out), .out(shifter_1_out));
  Shifter_part #(.width(16), .shift("lr")) shifter_2 (.in(in_1), .\dist (bit_extender_1_out), .out(shifter_2_out));
  Shifter_part #(.width(16), .shift("ar")) shifter_3 (.in(in_1), .\dist (bit_extender_1_out), .out(shifter_3_out));
  Multiplexer #(.select(2), .width(16)) multiplexer_1 (
    .in0(shifter_1_out), .in1(shifter_2_out), .in2(shifter_3_out), .out(Output), .sel(F));  // open: in3, en

  // Notes on the sheet:
  //   A
  //   B
endmodule

module CPU (
  input  [1:0] in_1,
  input  [1:0] in_2
);

  wire CLOCK;
  wire [1:0] F;
  wire [2:0] multiplexer_2_out, RD, Rs1, RS2;
  wire [4:0] imm2u_imm3l, imm5, OP;
  wire [10:0] imm11;
  wire [15:0] ALU_Output, bit_extender_1_out, bit_extender_2_out, bit_extender_3_out, bit_extender_4_out,
       BusA, BusB, BusW, Data_Memory_Output, multiplexer_1_out, multiplexer_3_out, multiplexer_4_out,
       Output_0, Output_1, Output_2, Output_3, PC, PC_1;

  Clock clock_1 (.out(CLOCK));
  PC_Normal_Adder pc_normal_adder_1 (.in_1(PC), .out_2(Output_0));
  Multiplexer #(.select(2), .width(16), .enable("false")) multiplexer_1 (
    .in0(Output_0), .in1(Output_1), .in2(Output_2), .in3(Output_3), .out(multiplexer_1_out), .sel(in_1));
  Jump_PC jump_pc_1 (.PC(PC), .imm11(imm11), .Output(Output_1));
  Register #(.width(16)) register_1 (.D(multiplexer_1_out), .en(1'b1), .Q(PC), .clr(CLOCK));  // open: clk
  Instruction_Memory instruction_memory_1 (
    .PC(PC), .imm2u_imm3l(imm2u_imm3l), .OP(OP), .Rd(RD), .Rs1(Rs1), .Rs2(RS2), .f(F), .imm11(imm11),
    .imm5(imm5));
  Branch_PC branch_pc_1 (.PC(PC), .imm2u_imm3l(imm2u_imm3l), .Output(Output_2));
  JALR_PC jalr_pc_1 (.imm5(imm5), .Output(Output_3));  // open: BusA
  Multiplexer #(.select(2), .width(3), .enable("false")) multiplexer_2 (
    .in0(RD), .in1(3'b001), .in2(3'b111), .out(multiplexer_2_out), .sel(in_2));  // open: in3
  Register_File register_file_1 (
    .BusW(BusW), .RD(multiplexer_2_out), .BusA(BusA), .Rs1(Rs1), .BusB(BusB), .Rs2(RS2), .RegWrite(1'b1),
    .Cllock(CLOCK));
  assign bit_extender_1_out = {{11{imm2u_imm3l[4]}}, imm2u_imm3l};  // Bit_Extender bit_extender_1
  assign bit_extender_2_out = {{5{imm11[10]}}, imm11};  // Bit_Extender bit_extender_2
  assign bit_extender_3_out = {{11{1'b0}}, imm5};  // Bit_Extender bit_extender_3
  Multiplexer #(.width(16), .enable("false")) multiplexer_3 (
    .in0(bit_extender_3_out), .in1(bit_extender_4_out), .out(multiplexer_3_out), .sel(1'b1));
  assign bit_extender_4_out = {{11{imm5[4]}}, imm5};  // Bit_Extender bit_extender_4
  Multiplexer #(.select(2), .width(16), .enable("false")) multiplexer_4 (
    .in0(BusB), .in1(bit_extender_2_out), .in2(bit_extender_1_out), .in3(multiplexer_3_out),
    .out(multiplexer_4_out), .sel(2'b11));
  ALU alu_1 (.in_1(BusA), .in_2(multiplexer_4_out), .F(F), .OP(OP), .Output(ALU_Output));
  Data_memory data_memory_1 (
    .address(ALU_Output), .data_in(BusB), .data_out(Data_Memory_Output), .MemRD(1'b1), .clock(CLOCK),
    .MemWR(1'b0));
  Multiplexer #(.select(2), .width(16), .enable("false")) multiplexer_5 (
    .in0(ALU_Output), .in1(Data_Memory_Output), .in2(PC_1), .out(BusW), .sel(2'b11));  // open: in3
endmodule

module ALU (
  input  [15:0] in_1,
  input  [15:0] in_2,
  input  [1:0] F,
  input  [4:0] OP,
  output [15:0] Output
);

  wire [1:0] multiplexer_1_out, multiplexer_3_out;
  wire [15:0] arithematic_1_output, logic_gate_1_output, shifter_1_output;

  Multiplexer #(.select(4), .width(2), .enable("false")) multiplexer_1 (
    .in0(F), .in1(F), .in2(F), .in3(2'b00), .in4(2'b10), .in5(2'b11), .in6(2'b00), .in7(2'b01), .in8(2'b10),
    .in9(2'b00), .in10(2'b01), .in11(2'b10), .out(multiplexer_1_out), .sel(OP[3:0]));  // open: in12, in13, in14, in15
  Logic_Gate logic_gate_1 (.in_1(in_1), .in_2(in_2), .F(multiplexer_1_out), .\output (logic_gate_1_output));
  Shifter shifter_1 (.in_1(in_1), .in_2(in_2), .F(multiplexer_1_out), .Output(shifter_1_output));
  Arithematic arithematic_1 (.in_1(in_1), .in_2(in_2), .F(multiplexer_1_out), .Output(arithematic_1_output));
  Multiplexer #(.select(2), .width(16), .enable("false")) multiplexer_2 (
    .in0(logic_gate_1_output), .in1(shifter_1_output), .in2(arithematic_1_output), .out(Output),
    .sel(multiplexer_3_out));  // open: in3
  Multiplexer #(.select(4), .width(2), .enable("false")) multiplexer_3 (
    .in0(2'b00), .in1(2'b01), .in2(2'b10), .in3(2'b10), .in4(2'b10), .in5(2'b10), .in6(2'b00), .in7(2'b00),
    .in8(2'b00), .in9(2'b01), .in10(2'b01), .in11(2'b01), .out(multiplexer_3_out), .sel(OP[3:0]));  // open: in12, in13, in14, in15

  // Notes on the sheet:
  //   A
  //   B
endmodule

module Instruction_Memory (
  input  [15:0] PC,
  output [4:0] OP,
  output [2:0] Rd,
  output [2:0] Rs1,
  output [2:0] Rs2,
  output [1:0] f,
  output [10:0] imm11,
  output [4:0] imm2u_imm3l,
  output [4:0] imm5
);

  ROM #(.addrWidth(16), .dataWidth(16)) rom_1 (
    .addr(PC), .data({f, imm5[2:0], imm11[5:3], imm2u_imm3l[2:0], OP}));  // open: sel

  assign imm2u_imm3l[4:3] = f;
  assign imm5[4:3] = f;
  assign {imm11[10:6], imm11[2:0]} = {f, imm5[2:0], imm2u_imm3l[2:0]};
  assign Rd = imm2u_imm3l[2:0];
  assign Rs1 = imm11[5:3];
  assign Rs2 = imm5[2:0];
endmodule

module Data_memory (
  input  [15:0] address,
  input  [15:0] data_in,
  input  clock,
  input  MemRD,
  input  MemWR,
  output [15:0] data_out
);

  RAM #(.addrWidth(16), .dataWidth(16), .bus("separate")) ram_1 (
    .addr(address), .din(data_in), .data(data_out), .str(MemRD), .clk(clock), .ld(MemWR));  // open: sel, clr
endmodule

module PC_Normal_Adder (
  input  [15:0] in_1,
  output [15:0] out_2
);

  Adder #(.width(16)) adder_1 (.a(16'h1), .b(in_1), .out(out_2));  // open: cin, cout
endmodule

module Jump_PC (
  input  [15:0] PC,
  input  [10:0] imm11,
  output [15:0] Output
);

  wire [15:0] bit_extender_1_out;

  assign bit_extender_1_out = {{5{imm11[10]}}, imm11};  // Bit_Extender bit_extender_1
  Adder #(.width(16)) adder_1 (.a(PC), .b(bit_extender_1_out), .out(Output));  // open: cin, cout
endmodule

module Branch_PC (
  input  [15:0] PC,
  input  [4:0] imm2u_imm3l,
  output [15:0] Output
);

  wire [15:0] bit_extender_1_out;

  assign bit_extender_1_out = {{11{1'b0}}, imm2u_imm3l};  // Bit_Extender bit_extender_1
  Adder #(.width(16)) adder_1 (.a(PC), .b(bit_extender_1_out), .out(Output));  // open: cin, cout
endmodule

module JALR_PC (
  input  [15:0] BusA,
  input  [4:0] imm5,
  output [15:0] Output
);

  wire [15:0] bit_extender_1_out;

  assign bit_extender_1_out = {{11{imm5[4]}}, imm5};  // Bit_Extender bit_extender_1
  Adder #(.width(16)) adder_1 (.a(BusA), .b(bit_extender_1_out), .out(Output));  // open: cin, cout
endmodule
